# Fritzing sketch schematics (saved by Fritzing 0.9.3b)
breadboards: 1

parts:
  Onderdeel1 = Arduino Uno (Rev3)
  Onderdeel2 = Matrix LED de 8x8 basada en MAX7219
  J1 = Piezo Speaker
  5V_bc_of_breakout_board = ESP8266 WiFi Module [part_number=ESP8266]
  R1 = Resistor [tolerance=±5% resistance=220 package="0805 [SMD]"]
  NTC_temperature_sensor = Temperature Sensor (Thermistor) [part_number="Epcos B57540G0104J" package=THT]
  Onderdeel3 = songle relay
  R2 = Resistor [tolerance=±5% resistance=1.5k package="0805 [SMD]"]
  D1 = Diode [package=diode-1n4148]
  npn_not_correct = NPN-Transistor [package="TO92 [THT]"]

nets:
  N1: Onderdeel1.A0, R1.Pin_1, NTC_temperature_sensor.pin_0
  N2: Onderdeel1.D10_PWM/SS, Onderdeel2.CS
  N3: Onderdeel1.D11_PWM/MOSI, Onderdeel2.CLK
  N4: Onderdeel1.D12/MISO, Onderdeel2.DIN
  N5: Onderdeel1.AREF, Onderdeel1.3V3, R1.Pin_0
  N6: Onderdeel1.D2, J1.pin2
  N7: Onderdeel1.D4, R2.Pin_1
  N8: Onderdeel1.D6_PWM, 5V_bc_of_breakout_board.TX
  N9: Onderdeel1.D7, 5V_bc_of_breakout_board.RX
  VCC: Onderdeel1.5V, Onderdeel2.VCC, 5V_bc_of_breakout_board.3.3V, Onderdeel3.VCC, D1.C
  GND: Onderdeel1.GND, Onderdeel2.GND, J1.pin1, 5V_bc_of_breakout_board.GND, NTC_temperature_sensor.pin_1, npn_not_correct.B
  N10: Onderdeel3.GND, D1.A, npn_not_correct.E
  N11: R2.Pin_0, npn_not_correct.C

custom parts:
  Temperature Sensor (Thermistor): A 100k NTC Thermistor (Temperature Sensor)
